# Fritzing sketch robotito_bluetooth (saved by Fritzing 0.9.3b)

parts:
  M1 = BTS7960
  Part1 = Arduino Nano (Rev3.0)
  U1 = LIPO-2000mAh [package=lipo-2000]
  M3 = DC Motor
  U2 = L298_BRIDGE_DRIVER [package=powerso20]
  M4 = DC Motor
  U3 = LIPO-2000mAh [package=lipo-2000]
  BT1 = Bluetooth HC-06u [package=THT]
  S1 = SPST Switch [package=switch-spdt]
  S2 = SPST Switch [package=switch-spdt]

nets:
  N1: M1.pin1, Part1.D10
  N2: M1.pin2, Part1.D9
  N3: M1.pin3, Part1.D7
  N4: M1.pin4, Part1.D8
  N5: M1.pin8, U2.GND
  N6: M1.pin11, S2.S
  N7: M1.pin12, U1.-
  GND: Part1.GND, BT1.GND
  N8: Part1.D2, U2.IN1
  N9: Part1.D3, U2.ENA
  N10: Part1.D4, U2.IN2
  N11: Part1.D5, BT1.RXD
  N12: Part1.D6, BT1.TXD
  N13: Part1.D11/MOSI, U2.ENB
  N14: Part1.D12/MISO, U2.IN4
  VIN: Part1.VIN, U2.VSS
  3V3: Part1.3V3, BT1.VCC
  N15: Part1.D13/SCK, U2.IN3
  N16: U1.+, S2.P
  N17: M3.pin_1, U2.OUT2
  N18: M3.pin_2, U2.OUT1
  N19: U2.VS, S1.O
  N20: U2.OUT3, M4.pin_1
  N21: U2.OUT4, M4.pin_2
  N22: U3.+, S1.P

custom parts:
  BTS7960: BTS7960 43A Peak Power H-Bridge PWM Motor Driver
  Bluetooth HC-06u: Bluetooth HC-06 - face up, pins down 16.5mm x 37.5mm PCB
